// Logisim project a.circ as structural Verilog: 4 circuits, main circuit main
// aoeu
module main (
  input  A,
  input  B,
  input  C,
  input  D,
  input  A_2,
  input  B_2,
  input  C_2,
  input  D_2,
  input  E,
  output AB,
  output C_D,
  output AB__prime,
  output C_D_2
);

  and and_1 (AB, A, B);
  or or_1 (C_D, C, D);
  nand nand_1 (AB__prime, A_2, B_2);
  nor nor_1 (C_D_2, C_2, ~D_2, E);  // NOR_Gate
endmodule

module comb (
  input  A,
  input  B,
  input  C,
  output out_4
);

  wire and_1_out, not_1_out;

  or or_1 (out_4, and_1_out, not_1_out);
  and and_1 (and_1_out, B, A);
  not not_1 (not_1_out, C);
endmodule

module gates (
  input  _0_A,
  input  _0_B,
  input  _0_C,
  input  _1_A,
  input  _1_B,
  input  _1_C,
  input  _2_A,
  input  _2_B,
  input  _2_C,
  input  _3_A,
  input  _3_B,
  input  _3_C,
  input  _4_A,
  input  _4_B,
  input  _4_C,
  input  _5_A,
  input  _5_B,
  input  _5_C,
  input  _6,
  output _0,
  output _1,
  output _2,
  output _3,
  output _4,
  output _5,
  output _6_2
);

  and and_1 (_0, _0_A, ~_0_B, _0_C);  // AND_Gate
  nand nand_1 (_1, _1_A, ~_1_B, _1_C);  // NAND_Gate
  or or_1 (_2, _2_A, ~_2_B, _2_C);  // OR_Gate
  nor nor_1 (_3, _3_A, ~_3_B, _3_C);  // NOR_Gate
  ExactlyOne xor_1 (.out(_4), .in0(_4_A), .in2(_4_B), .in4(_4_C));
  NotExactlyOne xnor_1 (.out(_5), .in0(_5_A), .in2(_5_B), .in4(_5_C));
  not not_1 (_6_2, _6);
endmodule

module splitters (
  input  [1:0] Input,
  output A,
  output B
);


  assign A = Input[0];
  assign B = Input[1];
endmodule
