// Logisim project memory.circ as structural Verilog: 2 circuits, main circuit register
module register (
  input  Edge_Clock,
  input  Edge_In,
  input  Edge_Load,
  input  Edge_Clear,
  input  Level_Clock,
  input  Level_In,
  input  Level_Load,
  input  Level_Clear,
  output R_Edge_Out,
  output F_Edge_Out,
  output H_Level_Out,
  output L_Level_Out
);

  Register #(.width(1)) register_1 (.D(Edge_In), .en(Edge_Load), .Q(R_Edge_Out), .clk(Edge_Clock), .clr(Edge_Clear));
  Register #(.width(1), .trigger("falling")) register_2 (
    .D(Edge_In), .en(Edge_Load), .Q(F_Edge_Out), .clk(Edge_Clock), .clr(Edge_Clear));
  Register #(.width(1), .trigger("high")) register_3 (
    .D(Level_In), .en(Level_Load), .Q(H_Level_Out), .clk(Level_Clock), .clr(Level_Clear));
  Register #(.width(1), .trigger("low")) register_4 (
    .D(Level_In), .en(Level_Load), .Q(L_Level_Out), .clk(Level_Clock), .clr(Level_Clear));
endmodule

module flip_flops (
  input  D_Edge_Clock,
  input  D_Edge_Data,
  input  D_Edge_Clear,
  input  D_Edge_Load,
  input  D_Edge_Preset,
  output D_R_Edge_Q1,
  output D_R_Edge_Q0,
  output D_F_Edge_Q1,
  output D_F_Edge_Q0
);

  D_Flip_Flop d_ff_1 (
    .clk(D_Edge_Clock), .D(D_Edge_Data), .Q(D_R_Edge_Q1), .Qn(D_R_Edge_Q0), .preset(D_Edge_Preset),
    .en(D_Edge_Load), .reset(D_Edge_Clear));
  T_Flip_Flop #(.trigger("falling")) t_ff_1 (
    .clk(D_Edge_Clock), .T(D_Edge_Data), .Q(D_F_Edge_Q1), .Qn(D_F_Edge_Q0), .preset(D_Edge_Preset),
    .reset(D_Edge_Clear), .en(D_Edge_Load));
endmodule
